# Fritzing sketch SevenSegment (saved by Fritzing 0.9.3b)
circuit board: 5.3807cm x 7.60952cm
breadboards: 1

parts:
  Ra = Resistor [tolerance=±5% resistance=220 package=THT]
  Rb = Resistor [tolerance=±5% resistance=220 package=THT]
  Rf = Resistor [tolerance=±5% resistance=220 package=THT]
  Rg = Resistor [tolerance=±5% resistance=220 package=THT]
  Rdp = Resistor [tolerance=±5% resistance=220 package=THT]
  Rc = Resistor [tolerance=±5% resistance=220 package=THT]
  Re = Resistor [tolerance=±5% resistance=220 package=THT]
  Part1 = Arduino Uno (Rev3)
  7_Segment1 = 7 Segment Display
  Rd = Resistor [tolerance=±5% resistance=220 package=THT]

nets:
  N1: Ra.Pin_0, Part1.D2
  N2: Ra.Pin_1, 7_Segment1.Segment_A
  N3: Rb.Pin_0, Part1.D3_PWM
  N4: Rb.Pin_1, 7_Segment1.Segment_B
  N5: Rf.Pin_0, Part1.D7
  N6: Rf.Pin_1, 7_Segment1.Segment_F
  N7: Rg.Pin_0, Part1.D8
  N8: Rg.Pin_1, 7_Segment1.Segment_G
  N9: Rdp.Pin_0, Part1.D9_PWM
  N10: Rdp.Pin_1, 7_Segment1.Segment_DP
  N11: Rc.Pin_0, Part1.D4
  N12: Rc.Pin_1, 7_Segment1.Segment_C
  N13: Re.Pin_0, Part1.D6_PWM
  N14: Re.Pin_1, 7_Segment1.Segment_E
  N15: Part1.D5_PWM, Rd.Pin_0
  N16: Part1.5V, 7_Segment1.common_anode
  N17: 7_Segment1.Segment_D, Rd.Pin_1
